# Fritzing sketch v0.1.1 (saved by Fritzing 0.9.2b)

parts:
  Часть1 = Arduino Nano (Rev3.0)
  LCD1 = LCD screen
  T1 = DS18B20 Temperature Sensor [part_number=DS18B20 package="TO92 [THT]"]
  T3 = DS18B20 Temperature Sensor [part_number=DS18B20 package="TO92 [THT]"]
  T4 = DS18B20 Temperature Sensor [part_number=DS18B20 package="TO92 [THT]"]
  T5 = DS18B20 Temperature Sensor [part_number=DS18B20 package="TO92 [THT]"]
  T6 = DS18B20 Temperature Sensor [part_number=DS18B20 package="TO92 [THT]"]
  T7 = DS18B20 Temperature Sensor [part_number=DS18B20 package="TO92 [THT]"]
  T8 = DS18B20 Temperature Sensor [part_number=DS18B20 package="TO92 [THT]"]
  T9 = DS18B20 Temperature Sensor [part_number=DS18B20 package="TO92 [THT]"]
  R1 = Resistor [tolerance=±5% resistance=220 package=THT]
  SW1 = DIP Switch 8 Position [package=dipswitch-08]
  ENT = Pushbutton [package="[THT]"]
  RST = Pushbutton [package="[THT]"]
  DOWN = Pushbutton [package="[THT]"]
  UP = Pushbutton [package="[THT]"]
  R3 = Resistor [tolerance=±5% resistance=220 package=THT]
  R4 = Resistor [tolerance=±5% resistance=220 package=THT]
  R5 = Resistor [tolerance=±5% resistance=220 package=THT]
  R2 = Resistor [tolerance=±5% resistance=220 package=THT]
  Left = Pushbutton [package="[THT]"]
  Right = Pushbutton [package="[THT]"]
  R6 = Resistor [tolerance=±5% resistance=220 package=THT]
  R8 = Resistor [tolerance=±5% resistance=220 package=THT]
  R7 = Resistor [tolerance=±5% resistance=220 package=THT]

nets:
  GND: Часть1.GND, LCD1.VSS, LCD1.R/W, LCD1.LED-, T1.+Vdd, T3.+Vdd, T4.+Vdd, T5.+Vdd, T6.+Vdd, T7.+Vdd, T8.+Vdd, T9.+Vdd, RST.Pin_1, RST.Pin_2, R3.Pin_1, R6.Pin_1
  N1: Часть1.D2, LCD1.DB4
  N2: Часть1.D3, LCD1.DB5
  N3: Часть1.D4, LCD1.DB6
  N4: Часть1.D5, LCD1.DB7
  N5: Часть1.D6, T1.DQ, T3.DQ, T4.DQ, T5.DQ, T6.DQ, T7.DQ, T8.DQ, T9.DQ, R1.Pin_0
  N6: Часть1.D7, SW1.8
  N7: Часть1.D8, SW1.7
  N8: Часть1.D9, SW1.6
  N9: Часть1.D10, SW1.5
  N10: Часть1.D11/MOSI, SW1.4
  N11: Часть1.D12/MISO, SW1.3
  N12: Часть1.RESET, RST.Pin_3, RST.Pin_4
  5V: Часть1.5V, LCD1.VDD, LCD1.LED+, R5.Pin_0, R7.Pin_0
  N13: Часть1.A7, ENT.Pin_3, DOWN.Pin_3, UP.Pin_3, UP.Pin_4
  N14: Часть1.A6, Left.Pin_1, Left.Pin_2, Right.Pin_1, Right.Pin_2
  N15: Часть1.A2, LCD1.RS
  N16: Часть1.A1, LCD1.E
  N17: Часть1.A0, SW1.1
  N18: Часть1.D13/SCK, SW1.2
  GND_2: T1.GND, T3.GND, T4.GND, T5.GND, T6.GND, T7.GND, T8.GND, T9.GND, R1.Pin_1
  N19: ENT.Pin_1, ENT.Pin_2, R4.Pin_0, R2.Pin_1
  N20: DOWN.Pin_1, DOWN.Pin_2, R3.Pin_0, R4.Pin_1
  N21: UP.Pin_2, R5.Pin_1, R2.Pin_0
  N22: Left.Pin_3, Left.Pin_4, R6.Pin_0, R8.Pin_1
  N23: Right.Pin_3, Right.Pin_4, R8.Pin_0, R7.Pin_1

custom parts:
  DS18B20 Temperature Sensor: A DS18B20 temperature sensor
